// Logisim project controller_example.circ as structural Verilog: 2 circuits, main circuit main
module main (
);

  wire ADD, ADDI, AND, Fake_ALU_out_2, Fake_ALU_out_3, Fake_ALU_out_4, Fake_ALU_out_5, LW, OR, or_1_out,
       or_2_out, or_3_out, or_4_out, SUB, SUBI, SW;
  wire [1:0] ALUOp;

  Button button_1 (.out(AND));
  Button button_2 (.out(OR));
  Button button_3 (.out(ADD));
  Button button_4 (.out(ADDI));
  Button button_5 (.out(SUB));
  Button button_6 (.out(SUBI));
  Button button_7 (.out(LW));
  Button button_8 (.out(SW));
  or or_1 (or_1_out, ADD, ADDI, LW, SW);
  or or_2 (or_2_out, SUB, SUBI);
  Priority_Encoder #(.select(2)) priority_encoder_1 (
    .in0(1'b1), .in1(OR), .in2(or_1_out), .in3(or_2_out), .out(ALUOp));  // open: gs, en_out, en_in
  // Probe on ALUOp
  FakeALU Fake_ALU (
    .in_1(ALUOp), .out_2(Fake_ALU_out_2), .out_3(Fake_ALU_out_3), .out_4(Fake_ALU_out_4),
    .out_5(Fake_ALU_out_5));
  LED MemWrite (.in(SW));
  or or_3 (or_3_out, AND, OR, ADD, ADDI, SUB, SUBI, LW);
  LED RegWrite (.in(or_3_out));
  LED RegDataSrc (.in(LW));
  LED ALUSrc (.in(or_4_out));
  or or_4 (or_4_out, ADDI, SUBI, SW, LW);
  LED u_AND (.in(Fake_ALU_out_2));
  LED OR_5 (.in(Fake_ALU_out_3));
  LED u_ADD (.in(Fake_ALU_out_4));
  LED u_SUB (.in(Fake_ALU_out_5));
endmodule

module FakeALU (
  input  [1:0] in_1,
  output out_2,
  output out_3,
  output out_4,
  output out_5
);

  buf and_1 (out_2, ~in_1[1]);  // AND_Gate AND_Gate
  buf and_2 (out_3, in_1[0]);  // AND_Gate AND_Gate
  // AND_Gate and_3: pin names not known; wires that end beside it: in_1[1], in_1[0], in_1[1], out_4
  and and_4 (out_5, in_1[1], in_1[0]);
endmodule
