// Logisim project esp27_lab11a.circ as structural Verilog: 1 circuit, main circuit main
module main (
  input  [15:0] ReadData1,
  input  WriteEnable,
  input  [1:0] ReadRegister1,
  input  [1:0] WriteRegister,
  input  [15:0] ReadData2,
  input  Clock,
  input  [15:0] WriteData,
  input  [1:0] ReadRegister2
);

  wire demultiplexer_1_out0, demultiplexer_1_out1, demultiplexer_1_out2, demultiplexer_1_out3, undriven;
  wire [15:0] register_1_q, register_2_q, register_3_q, register_4_q;

  Demultiplexer #(.select(2)) demultiplexer_1 (
    .out0(demultiplexer_1_out0), .out1(demultiplexer_1_out1), .out2(demultiplexer_1_out2),
    .out3(demultiplexer_1_out3), .in(WriteEnable), .sel(WriteRegister));  // open: en
  Register #(.width(16)) register_1 (
    .D(WriteData), .en(demultiplexer_1_out0), .Q(register_1_q), .clk(Clock));  // open: clr
  Register #(.width(16)) register_2 (
    .D(WriteData), .en(demultiplexer_1_out1), .Q(register_2_q), .clk(Clock));  // open: clr
  Register #(.width(16)) register_3 (
    .D(WriteData), .en(demultiplexer_1_out2), .Q(register_3_q), .clk(Clock));  // open: clr
  Register #(.width(16)) register_4 (
    .D(WriteData), .en(demultiplexer_1_out3), .Q(register_4_q), .clk(Clock), .clr(undriven));
  Register #(.width(16)) register_5 (
    .D(WriteData), .en(demultiplexer_1_out3), .Q(register_4_q), .clk(Clock), .clr(undriven));
  Multiplexer #(.select(2), .width(16)) multiplexer_1 (
    .in0(register_1_q), .in1(register_2_q), .in2(register_3_q), .in3(register_4_q), .out(ReadData1),
    .sel(ReadRegister1));  // open: en
  Multiplexer #(.select(2), .width(16)) multiplexer_2 (
    .in0(register_1_q), .in1(register_2_q), .in2(register_3_q), .in3(register_4_q), .out(ReadData2),
    .sel(ReadRegister2));  // open: en
endmodule
