// Logisim project esp27_lab11b.circ as structural Verilog: 1 circuit, main circuit main
module main (
);

  wire button_1_out, clock_1_out, comparator_2_eq, not_1_p1, not_1_p2;
  wire [3:0] counter_1_q, counter_2_q, counter_3_q, ram_1_data;

  Clock clock_1 (.out(clock_1_out));
  Counter #(.width(4), .max('hf)) counter_1 (.Q(counter_1_q), .clk(clock_1_out));  // open: load, D, count, carry, clr
  // NOT_Gate not_1: pin names not known; wires that end beside it: not_1_p1, not_1_p2
  Button button_1 (.out(button_1_out));
  RAM #(.addrWidth(4), .dataWidth(4)) ram_1 (
    .addr(counter_1_q), .data(ram_1_data), .clk(clock_1_out), .ld(not_1_p2), .clr(button_1_out));  // open: sel
  assign ram_1_data = not_1_p1 ? counter_2_q : 4'bz;  // Controlled_Buffer controlled_buffer_1
  Counter #(.width(4), .max('hf)) counter_2 (.Q(counter_2_q), .clk(clock_1_out));  // open: load, D, count, carry, clr
  Comparator #(.width(4)) comparator_1 (.a(4'b0000), .b(counter_3_q), .eq(not_1_p1));  // open: gt, lt
  Counter #(.width(4), .max('hf)) counter_3 (
    .D(4'b0000), .Q(counter_3_q), .clk(comparator_2_eq));  // open: load, count, carry, clr
  Comparator #(.width(4)) comparator_2 (.a(counter_2_q), .b(4'b0000), .eq(comparator_2_eq));  // open: gt, lt
endmodule
