// Logisim project picoMIPS.circ as structural Verilog: 4 circuits, main circuit main
module main (
);

  wire clock_1_out, control_1_select, fields_1_register, not_1_p2;
  wire [1:0] control_1_aluop;
  wire [3:0] fields_1_opcode;
  wire [7:0] adder_1_out, alu_1_result, fields_1_immediate, multiplexer_1_out, register_1_q, register_2_q,
       register_3_q;
  wire [15:0] rom_1_data;

  Clock clock_1 (.out(clock_1_out));
  Adder adder_1 (.a(8'h1), .b(register_1_q), .out(adder_1_out));  // open: cin, cout
  Register register_1 (.D(adder_1_out), .en(1'b1), .Q(register_1_q), .clk(clock_1_out));  // open: clr
  ROM #(.dataWidth(16)) rom_1 (.addr(register_1_q), .data(rom_1_data), .sel(1'b1));
  Fields fields_1 (
    .Instruction(rom_1_data), .Immediate(fields_1_immediate), .Register(fields_1_register),
    .Opcode(fields_1_opcode));
  // NOT_Gate not_1: pin names not known; wires that end beside it: fields_1_register, not_1_p2
  Control control_1 (.Opcode(fields_1_opcode), .ALUOp(control_1_aluop), .Select(control_1_select));
  Register register_2 (.D(multiplexer_1_out), .en(not_1_p2), .Q(register_2_q), .clk(clock_1_out));  // open: clr
  Register register_3 (
    .D(multiplexer_1_out), .en(fields_1_register), .Q(register_3_q), .clk(clock_1_out));  // open: clr
  ALU alu_1 (.A(register_2_q), .B(register_3_q), .Operation(control_1_aluop), .Result(alu_1_result));
  Multiplexer #(.width(8)) multiplexer_1 (
    .in0(alu_1_result), .in1(fields_1_immediate), .out(multiplexer_1_out), .sel(control_1_select));  // open: en

  // Notes on the sheet:
  //   contents of rom_1 (hex, n*v repeats v):
  //   1 802
endmodule

module ALU (
  input  [7:0] A,
  input  [7:0] B,
  input  [1:0] Operation,
  output [7:0] Result
);

  wire [7:0] adder_1_out, nand_1_out, nor_1_out, subtractor_1_out, undriven;

  Adder adder_1 (.a(A), .b(B), .out(adder_1_out));  // open: cin, cout
  Subtractor subtractor_1 (.a(A), .b(B), .out(subtractor_1_out));  // open: bin, bout
  assign nand_1_out = ~(A & B & undriven);  // NAND_Gate nand_1, 8 bits wide
  assign nor_1_out = ~(undriven | A | B);  // NOR_Gate nor_1, 8 bits wide
  Multiplexer #(.select(2), .width(8)) multiplexer_1 (
    .in0(adder_1_out), .in1(subtractor_1_out), .in2(nand_1_out), .in3(nor_1_out), .out(Result),
    .sel(Operation));  // open: en
endmodule

module Fields (
  input  [15:0] Instruction,
  output [7:0] Immediate,
  output Register,
  output [3:0] Opcode
);


  assign Immediate = Instruction[7:0];
  assign Opcode = Instruction[15:12];
  assign Register = Instruction[11];
endmodule

module Control (
  input  [3:0] Opcode,
  output [1:0] ALUOp,
  output Select
);

  wire add, and_1_out, and_2_out, and_3_out, \nand , \nor , not_2_p3, not_3_p4, not_4_p3, not_5_p3, not_6_p3,
       sub;
  wire [1:0] or_1_out;

  // NOT_Gate not_1: pin names not known; wires that end beside it: Opcode[2], or_1_out[1]
  // NOT_Gate not_2: pin names not known; wires that end beside it: Opcode[2], Opcode[0], not_2_p3
  // NOT_Gate not_3: pin names not known; wires that end beside it: Opcode[2], Opcode[0], Opcode[3], not_3_p4
  // NOT_Gate not_4: pin names not known; wires that end beside it: Opcode[0], Opcode[3], not_4_p3
  // NOT_Gate not_5: pin names not known; wires that end beside it: Opcode[3], Opcode[2], not_5_p3
  // NOT_Gate not_6: pin names not known; wires that end beside it: Opcode[3], Opcode[2], not_6_p3
  Decoder #(.select(4)) decoder_1 (
    .out0(Select), .out4(add), .out5(sub), .out8(\nor ), .out9(\nand ), .sel(Opcode));  // open: out1, out2, out3, out6, out7, out10, out11, out12, out13, out14, out15, en
  and and_1 (and_1_out, not_2_p3, not_3_p4);
  and and_2 (and_2_out, not_4_p3, Opcode[0]);
  and and_3 (and_3_out, not_5_p3, not_6_p3);
  or or_1 (or_1_out[0], and_1_out, and_2_out);
  // Probe on or_1_out
  // Probe on and_3_out
  Priority_Encoder #(.select(2)) priority_encoder_1 (
    .in0(1'b1), .in1(sub), .in2(\nand ), .in3(\nor ), .out(ALUOp));  // open: gs, en_out, en_in

  // Other names for the same wires on the sheet: set = Select

  // Notes on the sheet:
  //   Step 11.1 - Circuit designed with the Combinational Analysis tool
  //   Step 11.2 - Circuit designed with a decoder
endmodule
